// Logisim project LC3-2200a.circ as structural Verilog: 6 circuits, main circuit ALU
module Datapath (
  output [31:0] t2,
  output [31:0] sp,
  output [31:0] t1,
  output [31:0] t0,
  output [1:0] shiftmode,
  output [31:0] k0,
  output [31:0] a0,
  output [31:0] fp,
  output [31:0] s0,
  output [2:0] irbr,
  output [31:0] s2,
  output [2:0] gg,
  output [2:0] cond,
  output [31:0] s1,
  output br
);

  wire clk, DrALU, DrMEM, DrOFF, DrPc, DrREG, LdA, LdB, LdCC, LdIR, LdMAR, LdPc, not_1_out, WrMEM, WrREG;
  wire [1:0] func;
  wire [3:0] IR_q, IR_q_2, IR_q_3, IR_q_4, IR_q_5, IR_q_7, IR_q_8, RegNo;
  wire [3:3] IR_q_6;
  wire [19:0] bit_extender_2_out;
  wire [23:0] bit_extender_1_out;
  wire [31:0] A_q, alu_1_out, B_q, bit_extender_3_out, controlled_buffer_1_out, MAR_q, pc_q, ram_1_data,
       register_1_out;

  Clock clock_1 (.out(clk));
  Register_part #(.width(32)) pc (.D(controlled_buffer_1_out), .en(LdPc), .Q(pc_q), .clk(clk));  // open: clr
  assign controlled_buffer_1_out = DrPc ? pc_q : 32'bz;  // Controlled_Buffer controlled_buffer_1
  Comparator #(.width(32), .mode("unsigned")) comparator_1 (
    .a(controlled_buffer_1_out), .b({32{1'b0}}), .gt(gg[0]), .eq(gg[1]), .lt(gg[2]));
  Register_part #(.width(32)) A (.D(controlled_buffer_1_out), .en(LdA), .Q(A_q), .clk(clk));  // open: clr
  ALU alu_1 (.A(A_q), .B(B_q), .func(func), .out(alu_1_out), .shiftmode(shiftmode));  // open: out_5
  Register_part #(.width(32)) B (.D(controlled_buffer_1_out), .en(LdB), .Q(B_q), .clk(clk));  // open: clr
  assign controlled_buffer_1_out = DrALU ? alu_1_out : 32'bz;  // Controlled_Buffer controlled_buffer_2
  Register_part #(.width(3)) CC (.D(gg), .en(LdCC), .Q(cond), .clk(clk));  // open: clr
  nzpController nzpcontroller_1 (.IRNZP(irbr), .CurNZP(cond), .CCMatch(br));
  Register register_1 (
    .DIn(controlled_buffer_1_out), .clk(clk), .WrREG(WrREG), .RegNo(RegNo), .out(register_1_out), .k0(k0),
    .t0(t0), .t1(t1), .t2(t2), .s0(s0), .s1(s1), .s2(s2), .a0(a0), .sp(sp), .fp(fp));
  assign controlled_buffer_1_out = DrREG ? register_1_out : 32'bz;  // Controlled_Buffer controlled_buffer_3
  Register_part #(.width(32)) MAR (.D(controlled_buffer_1_out), .en(LdMAR), .Q(MAR_q), .clk(clk));  // open: clr
  Bit_Extender #(.in_width(32), .out_width(24)) bit_extender_1 (.in(MAR_q), .out(bit_extender_1_out));
  not not_1 (not_1_out, WrMEM);
  RAM #(.addrWidth(24), .dataWidth(32), .bus("separate")) ram_1 (
    .addr(bit_extender_1_out), .din(controlled_buffer_1_out), .data(ram_1_data), .str(WrMEM), .clk(clk),
    .ld(not_1_out));  // open: sel, clr
  assign controlled_buffer_1_out = DrMEM ? ram_1_data : 32'bz;  // Controlled_Buffer controlled_buffer_4
  Bit_Extender #(.in_width(32), .out_width(20)) bit_extender_2 (
    .in({IR_q_8, IR_q_7, IR_q_6[3], irbr, IR_q_5, IR_q_4, IR_q_3, IR_q_2, IR_q}), .out(bit_extender_2_out));
  assign bit_extender_3_out = {{12{bit_extender_2_out[19]}}, bit_extender_2_out};  // Bit_Extender bit_extender_3
  Register_part #(.width(32)) IR (
    .D(controlled_buffer_1_out), .en(LdIR),
    .Q({IR_q_8, IR_q_7, IR_q_6[3], irbr, IR_q_5, IR_q_4, IR_q_3, IR_q_2, IR_q}), .clk(clk));  // open: clr
  assign controlled_buffer_1_out = DrOFF ? bit_extender_3_out : 32'bz;  // Controlled_Buffer controlled_buffer_5
  Micro_sequencer micro_sequencer_1 (
    .IR({IR_q_8, IR_q_7, IR_q_6[3], irbr, IR_q_5, IR_q_4, IR_q_3, IR_q_2, IR_q}), .CCMatch(br), .LdA(LdA),
    .LdB(LdB), .LdCC(LdCC), .WrREG(WrREG), .WrMEM(WrMEM), .RegNo(RegNo), .func(func), .LdIR(LdIR),
    .LdPC(LdPc), .DrOFF(DrOFF), .DrPC(DrPc), .DrALU(DrALU), .DrMEM(DrMEM), .DrREG(DrREG), .LdMAR(LdMAR),
    .clk(clk));

  // Other names for the same wires on the sheet: nzp[2:0] = irbr; CCMatch = br
endmodule

module ALU (
  input  [31:0] A,
  input  [31:0] B,
  input  [1:0] func,
  output [31:0] out,
  output [4:0] out_5,
  output [1:0] shiftmode
);

  wire [31:0] adder_1_out, adder_2_out, and_1_out, multiplexer_1_out, not_1_out, shifter_1_out,
       shifter_2_out, shifter_3_out;

  Bit_Extender #(.in_width(32), .out_width(5)) bit_extender_1 (.in(B), .out(out_5));
  assign and_1_out = A & B;  // AND_Gate and_1, 32 bits wide
  Adder #(.width(32)) adder_1 (.a(A), .b(B), .out(adder_1_out));  // open: cin, cout
  assign not_1_out = ~and_1_out;  // NOT_Gate not_1, 32 bits wide
  Adder #(.width(32)) adder_2 (.a(A), .b(32'h1), .out(adder_2_out));  // open: cin, cout
  Shifter #(.width(32)) shifter_1 (.in(A), .\dist (out_5), .out(shifter_1_out));
  Shifter #(.width(32), .shift("lr")) shifter_2 (.in(A), .\dist (out_5), .out(shifter_2_out));
  Shifter #(.width(32), .shift("ar")) shifter_3 (.in(A), .\dist (out_5), .out(shifter_3_out));
  Multiplexer #(.select(2), .width(32), .disabled(0), .enable("false")) multiplexer_1 (
    .in0(shifter_1_out), .in1(shifter_2_out), .in2(shifter_1_out), .in3(shifter_3_out),
    .out(multiplexer_1_out), .sel(B[19:18]));
  Multiplexer #(.select(2), .width(32), .disabled(0), .enable("false")) multiplexer_2 (
    .in0(adder_1_out), .in1(not_1_out), .in2(adder_2_out), .in3(multiplexer_1_out), .out(out), .sel(func));

  assign shiftmode = B[19:18];

  // Other names for the same wires on the sheet: shift_mode[1:0] = B[19:18]
endmodule

// Micro Sequence
module Micro_sequencer (
  input  [31:0] IR,
  input  CCMatch,
  input  clk,
  output LdA,
  output LdB,
  output LdCC,
  output WrREG,
  output WrMEM,
  output [1:0] func,
  output LdIR,
  output LdPC,
  output DrOFF,
  output DrPC,
  output DrALU,
  output DrMEM,
  output DrREG,
  output LdMAR,
  output [3:0] RegNo
);

  wire CheckCC, OPTest;
  wire [1:0] RegSel;
  wire [5:0] IR_q, NextState, rom_2_data, rom_3_data, toIR;

  Register_part #(.width(6)) u_IR (.D(toIR), .en(1'b1), .Q(IR_q), .clk(clk));  // open: clr
  ROM #(.addrWidth(6), .dataWidth(25)) rom_1 (
    .addr(IR_q),
    .data({CheckCC, OPTest, func, RegSel, WrMEM, WrREG, LdCC, LdB, LdA, LdMAR, LdIR, LdPC, DrOFF, DrPC, DrALU, DrMEM, DrREG, NextState}));  // open: sel
  Multiplexer #(.select(2), .width(6), .disabled(0), .enable("false")) multiplexer_1 (
    .in0(NextState), .in1(rom_2_data), .in2(rom_3_data), .out(toIR), .sel({CheckCC, OPTest}));  // open: in3
  Multiplexer #(.select(2), .width(4), .disabled(0), .enable("false")) multiplexer_2 (
    .in0(IR[27:24]), .in1(IR[23:20]), .in2(IR[3:0]), .out(RegNo), .sel(RegSel));  // open: in3
  ROM #(.addrWidth(4), .dataWidth(6)) rom_2 (.addr(IR[31:28]), .data(rom_2_data));  // open: sel
  ROM #(.addrWidth(2), .dataWidth(6)) rom_3 (.addr({1'b0, CCMatch}), .data(rom_3_data));  // open: sel

  // Other names for the same wires on the sheet: Rz[3:0] = IR[3:0]; Ry[3:0] = IR[23:20]; Rx[3:0] = IR[27:24];
  //   OpCode[3:0] = IR[31:28]

  // Notes on the sheet:
  //   contents of rom_1 (hex, n*v repeats v):
  //   6201 1082 c00900 84044 108045 30100 84047 108408 30100 8404a 10804b 230100 2020d 80840 8404f 8410
  //   2111 30080 4213 8414 30100 84056 8417 2118 40040 8405a 841b 63011c 1d 0 5f 1000000 4221 8422 900 24
  //   23
  //   contents of rom_2 (hex, n*v repeats v):
  //   3 6 9 1e c e 12 15 19 6*0 23
  //   contents of rom_3 (hex, n*v repeats v):
  //   0 20
endmodule

module Register (
  input  [31:0] DIn,
  input  clk,
  input  WrREG,
  input  [3:0] RegNo,
  output [31:0] s0,
  output [31:0] k0,
  output [31:0] s1,
  output [31:0] a0,
  output [31:0] t0,
  output [31:0] out,
  output [31:0] sp,
  output [31:0] t1,
  output [31:0] fp,
  output [31:0] t2,
  output [31:0] s2
);

  wire _0Sel, _1Sel, _2Sel, _3Sel, _4Sel, _5Sel, _6Sel, _7Sel, _8Sel, _9Sel, _10Sel, _11Sel, _12Sel, _13Sel,
       _14Sel, _15Sel, decoder_1_out0, decoder_1_out1, decoder_1_out2, decoder_1_out3, decoder_1_out4,
       decoder_1_out5, decoder_1_out6, decoder_1_out7, decoder_1_out8, decoder_1_out9, decoder_1_out10,
       decoder_1_out11, decoder_1_out12, decoder_1_out13, decoder_1_out14, decoder_1_out15, not_1_out;
  wire [31:0] _0, _1, _2, _4, _5, _15;

  Multiplexer #(.select(4), .width(32), .disabled(0)) multiplexer_1 (
    .in0(_0), .in1(_1), .in2(_2), .in3(a0), .in4(_4), .in5(_5), .in6(t0), .in7(t1), .in8(t2), .in9(s0),
    .in10(s1), .in11(s2), .in12(k0), .in13(sp), .in14(fp), .in15(_15), .out(out), .sel(RegNo), .en(not_1_out));
  not not_1 (not_1_out, WrREG);
  Register_part #(.width(32)) u__0 (.D({32{1'b0}}), .en(_0Sel), .Q(_0), .clk(clk));  // open: clr
  Register_part #(.width(32)) _1__at (.D(DIn), .en(_1Sel), .Q(_1), .clk(clk));  // open: clr
  Register_part #(.width(32)) _2__v0 (.D(DIn), .en(_2Sel), .Q(_2), .clk(clk));  // open: clr
  Register_part #(.width(32)) _3_a0 (.D(DIn), .en(_3Sel), .Q(a0), .clk(clk));  // open: clr
  Register_part #(.width(32)) _4__a1 (.D(DIn), .en(_4Sel), .Q(_4), .clk(clk));  // open: clr
  Register_part #(.width(32)) _5__a2 (.D(DIn), .en(_5Sel), .Q(_5), .clk(clk));  // open: clr
  Register_part #(.width(32)) _6__t0 (.D(DIn), .en(_6Sel), .Q(t0), .clk(clk));  // open: clr
  Register_part #(.width(32)) _7__t1 (.D(DIn), .en(_7Sel), .Q(t1), .clk(clk));  // open: clr
  Register_part #(.width(32)) _8__t2 (.D(DIn), .en(_8Sel), .Q(t2), .clk(clk));  // open: clr
  Register_part #(.width(32)) _9__s0 (.D(DIn), .en(_9Sel), .Q(s0), .clk(clk));  // open: clr
  Register_part #(.width(32)) _10__s1 (.D(DIn), .en(_10Sel), .Q(s1), .clk(clk));  // open: clr
  Register_part #(.width(32)) _11__s2 (.D(DIn), .en(_11Sel), .Q(s2), .clk(clk));  // open: clr
  Register_part #(.width(32)) _12_k0 (.D(DIn), .en(_12Sel), .Q(k0), .clk(clk));  // open: clr
  Register_part #(.width(32)) _13_sp (.D(DIn), .en(_13Sel), .Q(sp), .clk(clk));  // open: clr
  Register_part #(.width(32)) _14_fp (.D(DIn), .en(_14Sel), .Q(fp), .clk(clk));  // open: clr
  Register_part #(.width(32)) _15_ra (.D(DIn), .en(_15Sel), .Q(_15), .clk(clk));  // open: clr
  Decoder #(.select(4), .enable("false")) decoder_1 (
    .out0(decoder_1_out0), .out1(decoder_1_out1), .out2(decoder_1_out2), .out3(decoder_1_out3),
    .out4(decoder_1_out4), .out5(decoder_1_out5), .out6(decoder_1_out6), .out7(decoder_1_out7),
    .out8(decoder_1_out8), .out9(decoder_1_out9), .out10(decoder_1_out10), .out11(decoder_1_out11),
    .out12(decoder_1_out12), .out13(decoder_1_out13), .out14(decoder_1_out14), .out15(decoder_1_out15),
    .sel(RegNo));
  and and_1 (_0Sel, decoder_1_out0, WrREG);
  and and_2 (_1Sel, decoder_1_out1, WrREG);
  and and_3 (_2Sel, decoder_1_out2, WrREG);
  and and_4 (_3Sel, decoder_1_out3, WrREG);
  and and_5 (_4Sel, decoder_1_out4, WrREG);
  and and_6 (_5Sel, decoder_1_out5, WrREG);
  and and_7 (_6Sel, decoder_1_out6, WrREG);
  and and_8 (_7Sel, decoder_1_out7, WrREG);
  and and_9 (_8Sel, decoder_1_out8, WrREG);
  and and_10 (_9Sel, decoder_1_out9, WrREG);
  and and_11 (_10Sel, decoder_1_out10, WrREG);
  and and_12 (_11Sel, decoder_1_out11, WrREG);
  and and_13 (_12Sel, decoder_1_out12, WrREG);
  and and_14 (_13Sel, decoder_1_out13, WrREG);
  and and_15 (_14Sel, decoder_1_out14, WrREG);
  and and_16 (_15Sel, decoder_1_out15, WrREG);

  // Other names for the same wires on the sheet: _3[31:0] = a0; _6[31:0] = t0; _7[31:0] = t1; _8[31:0] = t2;
  //   _9[31:0] = s0; _10[31:0] = s1; _11[31:0] = s2; _12[31:0] = k0; _13[31:0] = sp; _14[31:0] = fp;
  //   DataIn[31:0] = DIn; DataOut[31:0] = out
endmodule

module nzpController (
  input  [2:0] IRNZP,
  input  [2:0] CurNZP,
  output CCMatch
);

  wire and_1_out, and_2_out, and_3_out;

  and and_1 (and_1_out, CurNZP[0], IRNZP[0]);
  and and_2 (and_2_out, CurNZP[1], IRNZP[1]);
  and and_3 (and_3_out, CurNZP[2], IRNZP[2]);
  or or_1 (CCMatch, and_1_out, and_2_out, and_3_out);

  // Other names for the same wires on the sheet: CurP = CurNZP[0]; CurZ = CurNZP[1]; CurN = CurNZP[2]; IrP = IRNZP[0];
  //   IrZ = IRNZP[1]; IrN = IRNZP[2]
endmodule

module hehe (
  input  [2:0] in_1,
  output [2:0] shiftmode
);

  wire clock_1_out, undriven;

  Clock clock_1 (.out(clock_1_out));
  Register_part #(.width(3)) IR (.D(in_1), .en(undriven), .Q(shiftmode), .clk(clock_1_out));  // open: clr
endmodule
