// Logisim project YIHAN_ZHOU.circ as structural Verilog: 8 circuits, main circuit main
module main (
  output [31:0] out_1,
  output [31:0] fp,
  output [31:0] sp,
  output [31:0] at,
  output [31:0] s1,
  output pos_ex,
  output [31:0] out_7,
  output [31:0] out_8,
  output pos_mem,
  output [31:0] ra,
  output [31:0] s2,
  output pos_wb,
  output [31:0] t0,
  output [31:0] v0,
  output [3:0] out_15,
  output [31:0] t1,
  output [1:0] f2,
  output [1:0] out_18,
  output [3:0] out_19,
  output [3:0] out_20,
  output [1:0] f1,
  output [31:0] out_22,
  output [3:0] out_23,
  output [3:0] out_24,
  output [31:0] a0,
  output [31:0] out_26,
  output [3:0] out_27,
  output [31:0] out_28,
  output [31:0] t2,
  output [31:0] out_30,
  output [3:0] out_31,
  output [31:0] a1,
  output [31:0] k0,
  output [3:0] out_34,
  output [31:0] s0,
  output [31:0] out_36,
  output [31:0] out_37,
  output [31:0] out_38,
  output [31:0] out_39,
  output [31:0] a2,
  output [31:0] out_41,
  output [31:0] out_42,
  output [31:0] out_43
);

  wire and_1_out, and_3_out, and_4_out, and_5_out, and_6_out, BRANCH__EX, BRANCH__MEM, CLK, comparator_1_eq,
       comparator_2_eq, comparator_4_eq, comparator_5_eq, comparator_6_eq, comparator_7_eq, comparator_8_eq,
       comparator_9_eq, comparator_10_eq, comparator_11_gt, comparator_14_eq, comparator_15_eq,
       comparator_16_eq, comparator_17_eq, comparator_19_lt, comparator_20_gt, comparator_21_lt,
       comparator_22_eq, comparator_23_eq, comparator_24_eq, comparator_25_eq, comparator_26_eq,
       comparator_27_eq, comparator_28_eq, comparator_29_eq, comparator_32_eq, comparator_33_eq, EN, HALT,
       LDMEM_EX, LDMEM_MEM, LDREG_WB, LEA_WB, NOP, not_1_out, or_3_out, or_4_out, or_5_out, or_7_out, SQUASH,
       STALL, WREN, WRMEM_EX, WRMEM_MEM;
  wire [1:0] EX_FUNC_NO, or_1_out;
  wire [3:0] counter_1_q, idrr_ex_buffer_1_opcode_out, idrr_ex_buffer_1_rx_out, idrr_ex_buffer_1_ry_out,
       RX_EX, RX_IF, RX_MEM, RY_EX, RY_MEM, RY_WB, RZ_IF;
  wire [19:0] bit_extender_3_out;
  wire [19:4] if_idrr_buffer_1_ins_out;
  wire [23:0] bit_extender_1_out, bit_extender_2_out;
  wire [31:0] DATA_MEM, DATA_WB, idrr_ex_buffer_1_offset_out, idrr_ex_buffer_1_pc_out,
       idrr_ex_buffer_1_rdata1out, idrr_ex_buffer_1_rdata2out, multiplexer_12_out, OFFSET_EX, OFFSET_IF,
       OFFSET_MEM, passin_ex, PC_1, PC_1_EX, PC_1_IF, PC_1_MEM, PC_1_OFFSET_EX, PC_1_OFFSET_WB, PC_1_WB,
       PC_q, ram_1_data, RDATA2_MEM, RESULT_EX, RESULT_MEM, RESULT_WB;

  IDRR_EX_Buffer idrr_ex_buffer_1 (
    .Clear(SQUASH), .EN(EN), .Clock(CLK), .PC_IN(PC_1_IF), .Offset_IN(OFFSET_IF), .Rdata1IN(out_30),
    .Rdata2IN(out_36), .OPCODE_IN(out_19), .RX_IN(RX_IF), .RY_IN(out_20), .PC_OUT(idrr_ex_buffer_1_pc_out),
    .Offset_OUT(idrr_ex_buffer_1_offset_out), .Rdata1OUT(idrr_ex_buffer_1_rdata1out),
    .Rdata2OUT(idrr_ex_buffer_1_rdata2out), .OPCODE_OUT(idrr_ex_buffer_1_opcode_out),
    .RX_OUT(idrr_ex_buffer_1_rx_out), .RY_OUT(idrr_ex_buffer_1_ry_out));
  Multiplexer #(.select(2), .width(32)) multiplexer_1 (
    .in0(PC_1), .in1(out_1), .in2(out_22), .in3(PC_q), .out(out_7), .sel(out_18));  // open: en
  and and_1 (and_1_out, EN, not_1_out);
  EX_MEM_Buffer ex_mem_buffer_1 (
    .EN(1'b1), .Clock(CLK), .Offset_IN(OFFSET_EX), .Rdata1IN(out_38), .Rdata2_IN(out_42),
    .Result_IN(RESULT_EX), .OPCODE_EX(out_23), .Rx_In(RX_EX), .Ry_In(RY_EX), .PC_1_IN(PC_1_EX),
    .BRANCH(BRANCH__EX), .Pc_1_offset(PC_1_OFFSET_EX), .Offset_OUT(OFFSET_MEM), .Rdata1_OUT(out_22),
    .Rdata2_OUT(RDATA2_MEM), .Result_Out(RESULT_MEM), .OPCODE_EX_2(out_24), .Rx_OUT(RX_MEM), .Ry_OUT(RY_MEM),
    .PC_1_OUT(PC_1_MEM), .BRANCH_2(BRANCH__MEM), .Pc_1_offset_2(out_1), .WRMEM_IN(WRMEM_EX),
    .WRMEM_OUT(WRMEM_MEM), .LDMEM_IN(LDMEM_EX), .LDMEM_OUT(LDMEM_MEM));
  MEM_WB_Buffer mem_wb_buffer_1 (
    .EN(1'b1), .Clock(CLK), .PC_1_IN(PC_1_MEM), .Result_IN(RESULT_MEM), .DATA_IN(DATA_MEM),
    .OPCODE_IN(out_24), .Rx_In(RX_MEM), .Ry_In(RY_MEM), .PC_1_OUT(PC_1_WB), .Result_Out(RESULT_WB),
    .DATA_OUT(DATA_WB), .OPCODE_OUT(out_27), .Rx_OUT(out_15), .Ry_OUT(RY_WB), .PC_1_OFFSET_IN(out_1),
    .PC_1_OFFSET_OUT(PC_1_OFFSET_WB));
  Register #(.width(32)) PC (.D(out_7), .en(and_1_out), .Q(PC_q), .clk(CLK));  // open: clr
  not not_1 (not_1_out, HALT);
  Multiplexer #(.width(32)) multiplexer_2 (
    .in0(idrr_ex_buffer_1_pc_out), .in1({32{1'b0}}), .out(PC_1_EX), .sel(NOP));  // open: en
  Multiplexer #(.width(32)) multiplexer_3 (
    .in0(idrr_ex_buffer_1_offset_out), .in1({32{1'b0}}), .out(OFFSET_EX), .sel(NOP));  // open: en
  Multiplexer #(.width(32)) multiplexer_4 (
    .in0(idrr_ex_buffer_1_rdata1out), .in1({32{1'b0}}), .out(out_38), .sel(NOP));  // open: en
  Multiplexer #(.width(32)) multiplexer_5 (
    .in0(idrr_ex_buffer_1_rdata2out), .in1({32{1'b0}}), .out(out_42), .sel(NOP));  // open: en
  Multiplexer #(.width(4)) multiplexer_6 (
    .in0(idrr_ex_buffer_1_opcode_out), .in1(4'b0000), .out(out_23), .sel(NOP));  // open: en
  Multiplexer #(.width(4)) multiplexer_7 (
    .in0(idrr_ex_buffer_1_rx_out), .in1(4'b0000), .out(RX_EX), .sel(NOP));  // open: en
  Multiplexer #(.width(4)) multiplexer_8 (
    .in0(idrr_ex_buffer_1_ry_out), .in1(4'b0000), .out(RY_EX), .sel(NOP));  // open: en
  Bit_Extender #(.in_width(32), .out_width(24), .\type ("sign")) bit_extender_1 (.in(PC_q), .out(bit_extender_1_out));
  Adder #(.width(32)) adder_1 (.a(PC_q), .b(32'h1), .out(PC_1));  // open: cin, cout
  Comparator #(.width(4)) comparator_1 (.a(out_23), .b(4'b1111), .eq(comparator_1_eq));  // open: gt, lt
  Multiplexer multiplexer_9 (.in0(1'b1), .in1(1'b0), .out(EN), .sel(STALL));  // open: en
  Counter #(.width(4), .max('hf)) counter_1 (
    .count(comparator_1_eq), .Q(counter_1_q), .clk(CLK));  // open: load, D, carry, clr
  RAM #(.addrWidth(24), .dataWidth(32)) ram_1 (
    .addr(bit_extender_1_out), .data(ram_1_data), .clk(CLK));  // open: sel, ld, clr
  Comparator #(.width(2)) comparator_2 (.a(out_18), .b(2'b00), .eq(comparator_2_eq));  // open: gt, lt
  IF_IDRR_Buffer if_idrr_buffer_1 (
    .Clear(SQUASH), .EN(EN), .Clock(CLK), .PC_1(PC_1), .INS(out_28), .PC_1_OUT(PC_1_IF),
    .INS_OUT({out_19, RX_IF, out_20, if_idrr_buffer_1_ins_out, RZ_IF}));
  Multiplexer #(.width(32)) multiplexer_10 (.in0(ram_1_data), .in1({32{1'b0}}), .out(out_28), .sel(HALT));  // open: en
  Comparator #(.width(4)) comparator_3 (.a(counter_1_q), .b(4'b0000), .gt(HALT));  // open: eq, lt
  Register #(.width(1)) register_1 (.D(STALL), .en(1'b1), .Q(NOP), .clk(CLK));  // open: clr
  not not_2 (SQUASH, comparator_2_eq);
  Bit_Extender #(.in_width(32), .out_width(24), .\type ("sign")) bit_extender_2 (
    .in(RESULT_MEM), .out(bit_extender_2_out));
  Multiplexer #(.select(2), .width(32)) multiplexer_11 (
    .in0(RESULT_WB), .in1(DATA_WB), .in2(PC_1_WB), .in3(PC_1_OFFSET_WB), .out(out_37), .sel(or_1_out));  // open: en
  Comparator #(.width(4)) comparator_4 (.a(out_27), .b(4'b0100), .eq(comparator_4_eq));  // open: gt, lt
  Comparator #(.width(4)) comparator_5 (.a(out_20), .b(RX_EX), .eq(comparator_5_eq));  // open: gt, lt
  Comparator #(.width(4)) comparator_6 (.a(out_31), .b(RX_EX), .eq(comparator_6_eq));  // open: gt, lt
  or or_1 (or_1_out[0], LDREG_WB, LEA_WB);
  or or_2 (or_1_out[1], comparator_4_eq, LEA_WB);
  Bit_Extender #(.in_width(32), .out_width(20)) bit_extender_3 (
    .in({out_19, RX_IF, out_20, if_idrr_buffer_1_ins_out, RZ_IF}), .out(bit_extender_3_out));
  Comparator #(.width(4)) comparator_7 (.a(out_23), .b(4'b0101), .eq(comparator_7_eq));  // open: gt, lt
  Comparator #(.width(4)) comparator_8 (.a(out_23), .b(4'b0110), .eq(comparator_8_eq));  // open: gt, lt
  or or_3 (or_3_out, comparator_5_eq, comparator_6_eq);
  assign OFFSET_IF = {{12{bit_extender_3_out[19]}}, bit_extender_3_out};  // Bit_Extender bit_extender_4
  or or_4 (or_4_out, comparator_7_eq, comparator_8_eq);
  Comparator #(.width(4)) comparator_9 (.a(out_23), .b(4'b0000), .eq(comparator_9_eq));  // open: gt, lt
  Comparator #(.width(4)) comparator_10 (.a(out_23), .b(4'b0010), .eq(comparator_10_eq));  // open: gt, lt
  RAM #(.addrWidth(24), .dataWidth(32), .bus("separate")) ram_2 (
    .addr(bit_extender_2_out), .din(RDATA2_MEM), .data(DATA_MEM), .str(WRMEM_MEM), .clk(CLK), .ld(LDMEM_MEM));  // open: sel, clr
  and and_2 (STALL, or_4_out, or_3_out);
  or or_5 (or_5_out, comparator_9_eq, comparator_10_eq);
  Comparator #(.width(4), .mode("unsigned")) comparator_11 (
    .a(out_19), .b(4'b0010), .gt(comparator_11_gt));  // open: eq, lt
  Multiplexer #(.width(32)) multiplexer_12 (
    .in0(OFFSET_EX), .in1(out_42), .out(multiplexer_12_out), .sel(or_5_out));  // open: en
  Comparator #(.width(4)) comparator_12 (.a(out_27), .b(4'b0101), .eq(LDREG_WB));  // open: gt, lt
  Comparator #(.width(4)) comparator_13 (.a(out_27), .b(4'b0110), .eq(LEA_WB));  // open: gt, lt
  Clock Clock (.out(CLK));
  ALU ALU (.A(PC_1_EX), .B(OFFSET_EX), .func(2'b00), .out(PC_1_OFFSET_EX));  // open: out_5, shiftmode
  Multiplexer #(.width(4)) multiplexer_13 (.in0(RZ_IF), .in1(RX_IF), .out(out_31), .sel(comparator_11_gt));  // open: en
  ALU ALU_2 (.A(out_38), .B(multiplexer_12_out), .func(EX_FUNC_NO), .out(RESULT_EX));  // open: out_5, shiftmode
  Comparator #(.width(4)) comparator_14 (.a(out_23), .b(4'b0010), .eq(comparator_14_eq));  // open: gt, lt
  Comparator #(.width(4)) comparator_15 (.a(out_23), .b(4'b1000), .eq(comparator_15_eq));  // open: gt, lt
  Comparator #(.width(4)) comparator_16 (.a(out_24), .b(4'b0011), .eq(comparator_16_eq));  // open: gt, lt
  Comparator #(.width(4)) comparator_17 (.a(out_24), .b(4'b1001), .eq(comparator_17_eq));  // open: gt, lt
  or or_6 (EX_FUNC_NO[0], comparator_14_eq, comparator_15_eq);
  Comparator #(.width(4)) comparator_18 (.a(out_23), .b(4'b1000), .eq(EX_FUNC_NO[1]));  // open: gt, lt
  or or_7 (or_7_out, comparator_16_eq, comparator_17_eq);
  Comparator #(.width(4), .mode("unsigned")) comparator_19 (
    .a(out_27), .b(4'b0011), .lt(comparator_19_lt));  // open: gt, eq
  Comparator #(.width(4), .mode("unsigned")) comparator_20 (
    .a(out_27), .b(4'b0011), .gt(comparator_20_gt));  // open: eq, lt
  Comparator #(.width(4), .mode("unsigned")) comparator_21 (
    .a(out_27), .b(4'b0111), .lt(comparator_21_lt));  // open: gt, eq
  Comparator #(.width(4), .mode("unsigned")) comparator_22 (
    .a(out_27), .b(4'b1000), .eq(comparator_22_eq));  // open: gt, lt
  Comparator #(.width(4)) comparator_23 (.a(out_23), .b(4'b0011), .eq(comparator_23_eq));  // open: gt, lt
  Comparator #(.width(32)) comparator_24 (.a(out_38), .b(out_42), .eq(comparator_24_eq));  // open: gt, lt
  Comparator #(.width(32)) comparator_25 (.a(out_38), .b(out_42), .eq(comparator_25_eq));  // open: gt, lt
  Comparator #(.width(4)) comparator_26 (.a(out_23), .b(4'b1001), .eq(comparator_26_eq));  // open: gt, lt
  and and_3 (and_3_out, or_7_out, BRANCH__MEM);
  Comparator #(.width(4)) comparator_27 (.a(out_24), .b(4'b1111), .eq(comparator_27_eq));  // open: gt, lt
  Dual_Ported_Register_File dual_ported_register_file_1 (
    .CLK(CLK), .WrREGNO(out_15), .RdREGNO1(out_20), .RdREGNO2(out_31), .INPUT(out_37), .OUT1(out_8),
    .OUT2(out_39), .WrEN(WREN), .v0(v0), .a0(a0), .a1(a1), .a2(a2), .t0(t0), .t1(t1), .t2(t2), .s0(s0),
    .s1(s1), .s2(s2), .sp(sp), .fp(fp), .ra(ra), .k0(k0), .at(at));
  and and_4 (and_4_out, comparator_23_eq, comparator_24_eq);
  and and_5 (and_5_out, ~comparator_25_eq, comparator_26_eq);  // AND_Gate
  Comparator #(.width(4)) comparator_28 (.a(out_24), .b(4'b0100), .eq(comparator_28_eq));  // open: gt, lt
  Comparator #(.width(4)) comparator_29 (.a(out_24), .b(4'b1111), .eq(comparator_29_eq));  // open: gt, lt
  and and_6 (and_6_out, comparator_20_gt, comparator_21_lt);
  or or_8 (out_18[0], and_3_out, comparator_27_eq);
  or or_9 (BRANCH__EX, and_4_out, and_5_out);
  Comparator #(.width(4)) comparator_30 (.a(out_23), .b(4'b0101), .eq(LDMEM_EX));  // open: gt, lt
  Comparator #(.width(4)) comparator_31 (.a(out_23), .b(4'b0111), .eq(WRMEM_EX));  // open: gt, lt
  or or_10 (out_18[1], comparator_28_eq, comparator_29_eq);
  or or_11 (WREN, comparator_19_lt, and_6_out, comparator_22_eq);
  Multiplexer #(.width(32)) multiplexer_14 (
    .in0(RESULT_MEM), .in1(out_1), .out(out_26), .sel(comparator_32_eq));  // open: en
  Comparator #(.width(4)) comparator_32 (.a(out_24), .b(4'b0110), .eq(comparator_32_eq));  // open: gt, lt
  FORWARDING forwarding_1 (
    .Result_EX(passin_ex), .DATA_MEM(DATA_MEM), .OUT1(out_8), .Rx_EX(RX_EX), .OPCODE_IF(out_19),
    .Rx_MEM(RX_MEM), .OPCODE_EX(out_23), .Rx_WB(out_15), .Result_MEM(out_26), .OPCODE_MEM(out_24),
    .OPCODE_WB(out_27), .OUT2(out_39), .Ry_IDRR(out_20), .RSel_IDRR(out_31), .Result_WB(out_37),
    .FOUT2(out_36), .FOUT1(out_30), .f__dt1(f1), .f__dt2(f2), .pos_ex(pos_ex), .pos_mem(pos_mem),
    .pos_wb(pos_wb));  // open: wb_ffff, mem_ffff, out_16, out_17
  Multiplexer #(.width(32)) multiplexer_15 (
    .in0(RESULT_EX), .in1(PC_1_OFFSET_EX), .out(passin_ex), .sel(comparator_33_eq));  // open: en
  Comparator #(.width(4)) comparator_33 (.a(out_24), .b(4'b0110), .eq(comparator_33_eq));  // open: gt, lt

  assign out_34 = out_31;
  assign out_41 = out_38;
  assign out_43 = out_37;

  // Other names for the same wires on the sheet: RY_IF[3:0] = out_20; OPCODE_IF[3:0] = out_19; DPRF_IN[31:0] = out_37;
  //   FOUT1[31:0] = out_30; FOUT2[31:0] = out_36; OPCODE_EX[3:0] = out_23; OPCODE_MEM[3:0] = out_24;
  //   OPCODE_WB[3:0] = out_27; OUT1[31:0] = out_8; OUT2[31:0] = out_39; PC_1_OFFSET_MEM[31:0] = out_1;
  //   PC_SEL[1:0] = out_18; RDATA1_EX[31:0] = out_38; RDATA1_MEM[31:0] = out_22; RDATA2_EX[31:0] = out_42;
  //   REGSEL2[3:0] = out_31; RX_WB[3:0] = out_15; WRREGNO[3:0] = out_15
endmodule

module Dual_Ported_Register_File (
  input  CLK,
  input  WrEN,
  input  [3:0] WrREGNO,
  input  [3:0] RdREGNO1,
  input  [3:0] RdREGNO2,
  input  [31:0] INPUT,
  output [31:0] OUT1,
  output [31:0] v0,
  output [31:0] a0,
  output [31:0] sp,
  output [31:0] OUT2,
  output [31:0] a1,
  output [31:0] fp,
  output [31:0] a2,
  output [31:0] ra,
  output [31:0] t0,
  output [31:0] k0,
  output [31:0] t1,
  output [31:0] t2,
  output [31:0] at,
  output [31:0] s0,
  output [31:0] s1,
  output [31:0] s2
);

  wire En_a0, En_a1, En_a2, En_at, En_fp, En_k0, En_ra, En_s0, En_s1, En_s2, En_sp, En_t0, En_t1, En_t2,
       En_v0;
  wire [31:0] zero;

  Decoder #(.select(4), .disabled(0)) decoder_1 (
    .out1(En_at), .out2(En_v0), .out3(En_a0), .out4(En_a1), .out5(En_a2), .out6(En_t0), .out7(En_t1),
    .out8(En_t2), .out9(En_s0), .out10(En_s1), .out11(En_s2), .out12(En_k0), .out13(En_sp), .out14(En_fp),
    .out15(En_ra), .sel(WrREGNO), .en(WrEN));  // open: out0
  Register #(.width(32)) u_zero (.D(INPUT), .en(1'b0), .Q(zero), .clk(CLK));  // open: clr
  Register #(.width(32)) u_at (.D(INPUT), .en(En_at), .Q(at), .clk(CLK));  // open: clr
  Register #(.width(32)) u_v0 (.D(INPUT), .en(En_v0), .Q(v0), .clk(CLK));  // open: clr
  Register #(.width(32)) u_a0 (.D(INPUT), .en(En_a0), .Q(a0), .clk(CLK));  // open: clr
  Register #(.width(32)) u_a1 (.D(INPUT), .en(En_a1), .Q(a1), .clk(CLK));  // open: clr
  Register #(.width(32)) u_a2 (.D(INPUT), .en(En_a2), .Q(a2), .clk(CLK));  // open: clr
  Register #(.width(32)) a3 (.D(INPUT), .en(En_t0), .Q(t0), .clk(CLK));  // open: clr
  Register #(.width(32)) a4 (.D(INPUT), .en(En_t1), .Q(t1), .clk(CLK));  // open: clr
  Multiplexer #(.select(4), .width(32), .disabled(0), .enable("false")) multiplexer_1 (
    .in0(zero), .in1(at), .in2(v0), .in3(a0), .in4(a1), .in5(a2), .in6(t0), .in7(t1), .in8(t2), .in9(s0),
    .in10(s1), .in11(s2), .in12(k0), .in13(sp), .in14(fp), .in15(ra), .out(OUT2), .sel(RdREGNO2));
  Register #(.width(32)) u_s0 (.D(INPUT), .en(En_t2), .Q(t2), .clk(CLK));  // open: clr
  Register #(.width(32)) u_s1 (.D(INPUT), .en(En_s0), .Q(s0), .clk(CLK));  // open: clr
  Register #(.width(32)) u_s2 (.D(INPUT), .en(En_s1), .Q(s1), .clk(CLK));  // open: clr
  Register #(.width(32)) s3 (.D(INPUT), .en(En_s2), .Q(s2), .clk(CLK));  // open: clr
  Register #(.width(32)) u_k0 (.D(INPUT), .en(En_k0), .Q(k0), .clk(CLK));  // open: clr
  Register #(.width(32)) u_sp (.D(INPUT), .en(En_sp), .Q(sp), .clk(CLK));  // open: clr
  Register #(.width(32)) u_fp (.D(INPUT), .en(En_fp), .Q(fp), .clk(CLK));  // open: clr
  Register #(.width(32)) u_ra (.D(INPUT), .en(En_ra), .Q(ra), .clk(CLK));  // open: clr
  Multiplexer #(.select(4), .width(32), .disabled(0), .enable("false")) multiplexer_2 (
    .in0(zero), .in1(at), .in2(v0), .in3(a0), .in4(a1), .in5(a2), .in6(t0), .in7(t1), .in8(t2), .in9(s0),
    .in10(s1), .in11(s2), .in12(k0), .in13(sp), .in14(fp), .in15(ra), .out(OUT1), .sel(RdREGNO1));

  // Notes on the sheet:
  //   MODIFY AT YOUR OWN RISK
endmodule

// IF/IDRR BUF
module IF_IDRR_Buffer (
  input  Clear,
  input  EN,
  input  Clock,
  input  [31:0] PC_1,
  input  [31:0] INS,
  output [31:0] PC_1_OUT,
  output [31:0] INS_OUT
);

  Register #(.width(32)) PC (.D(PC_1), .en(EN), .Q(PC_1_OUT), .clk(Clock), .clr(Clear));
  Register #(.width(32)) Instruction (.D(INS), .en(EN), .Q(INS_OUT), .clk(Clock), .clr(Clear));

  // Other names for the same wires on the sheet: CLK = Clock; CLR = Clear
endmodule

// IDRR/EX BUF
module IDRR_EX_Buffer (
  input  Clear,
  input  EN,
  input  Clock,
  input  [31:0] PC_IN,
  input  [31:0] Offset_IN,
  input  [31:0] Rdata1IN,
  input  [31:0] Rdata2IN,
  input  [3:0] OPCODE_IN,
  input  [3:0] RX_IN,
  input  [3:0] RY_IN,
  output [31:0] PC_OUT,
  output [31:0] Offset_OUT,
  output [31:0] Rdata1OUT,
  output [31:0] Rdata2OUT,
  output [3:0] OPCODE_OUT,
  output [3:0] RX_OUT,
  output [3:0] RY_OUT
);

  Register #(.width(32)) PC (.D(PC_IN), .en(EN), .Q(PC_OUT), .clk(Clock), .clr(Clear));
  Register #(.width(32)) Offset (.D(Offset_IN), .en(EN), .Q(Offset_OUT), .clk(Clock), .clr(Clear));
  Register #(.width(32)) Rdata1 (.D(Rdata1IN), .en(EN), .Q(Rdata1OUT), .clk(Clock), .clr(Clear));
  Register #(.width(32)) Rdata2 (.D(Rdata2IN), .en(EN), .Q(Rdata2OUT), .clk(Clock), .clr(Clear));
  Register #(.width(4)) OPCODE (.D(OPCODE_IN), .en(EN), .Q(OPCODE_OUT), .clk(Clock), .clr(Clear));
  Register #(.width(4)) Rx (.D(RX_IN), .en(EN), .Q(RX_OUT), .clk(Clock), .clr(Clear));
  Register #(.width(4)) Ry (.D(RY_IN), .en(EN), .Q(RY_OUT), .clk(Clock), .clr(Clear));

  // Other names for the same wires on the sheet: CLK = Clock; CLR = Clear
endmodule

// EX/MEM BUF
module EX_MEM_Buffer (
  input  EN,
  input  Clock,
  input  [31:0] Offset_IN,
  input  [31:0] Rdata1IN,
  input  [31:0] Rdata2_IN,
  input  [31:0] Result_IN,
  input  [3:0] OPCODE_EX,
  input  [3:0] Rx_In,
  input  [3:0] Ry_In,
  input  [31:0] PC_1_IN,
  input  BRANCH,
  input  [31:0] Pc_1_offset,
  input  WRMEM_IN,
  input  LDMEM_IN,
  output [31:0] Offset_OUT,
  output [31:0] Rdata1_OUT,
  output [31:0] Rdata2_OUT,
  output [31:0] Result_Out,
  output [3:0] OPCODE_EX_2,
  output [3:0] Rx_OUT,
  output [3:0] Ry_OUT,
  output [31:0] PC_1_OUT,
  output BRANCH_2,
  output [31:0] Pc_1_offset_2,
  output WRMEM_OUT,
  output LDMEM_OUT
);

  Register #(.width(32)) Rdata2 (.D(Rdata2_IN), .en(EN), .Q(Rdata2_OUT), .clk(Clock));  // open: clr
  Register #(.width(32)) RESULT (.D(Result_IN), .en(EN), .Q(Result_Out), .clk(Clock));  // open: clr
  Register #(.width(4)) OPCODE (.D(OPCODE_EX), .en(EN), .Q(OPCODE_EX_2), .clk(Clock));  // open: clr
  Register #(.width(4)) Rx (.D(Rx_In), .en(EN), .Q(Rx_OUT), .clk(Clock));  // open: clr
  Register #(.width(4)) Ry (.D(Ry_In), .en(EN), .Q(Ry_OUT), .clk(Clock));  // open: clr
  Register #(.width(32)) PC_1 (.D(PC_1_IN), .en(EN), .Q(PC_1_OUT), .clk(Clock));  // open: clr
  Register #(.width(1)) u_BRANCH (.D(BRANCH), .en(EN), .Q(BRANCH_2), .clk(Clock));  // open: clr
  Register #(.width(32)) NEWPC (.D(Pc_1_offset), .en(EN), .Q(Pc_1_offset_2), .clk(Clock));  // open: clr
  Register #(.width(1)) WRMEM (.D(WRMEM_IN), .en(EN), .Q(WRMEM_OUT), .clk(Clock));  // open: clr
  Register #(.width(1)) LDMEM (.D(LDMEM_IN), .en(EN), .Q(LDMEM_OUT), .clk(Clock));  // open: clr
  Register #(.width(32)) Offset (.D(Offset_IN), .en(EN), .Q(Offset_OUT), .clk(Clock));  // open: clr
  Register #(.width(32)) Rdata1 (.D(Rdata1IN), .en(EN), .Q(Rdata1_OUT), .clk(Clock));  // open: clr

  // Other names for the same wires on the sheet: CLK = Clock
endmodule

// MEM/WB BUF
module MEM_WB_Buffer (
  input  EN,
  input  Clock,
  input  [31:0] PC_1_IN,
  input  [31:0] Result_IN,
  input  [31:0] DATA_IN,
  input  [3:0] OPCODE_IN,
  input  [3:0] Rx_In,
  input  [3:0] Ry_In,
  input  [31:0] PC_1_OFFSET_IN,
  output [31:0] PC_1_OUT,
  output [31:0] Result_Out,
  output [31:0] DATA_OUT,
  output [3:0] OPCODE_OUT,
  output [3:0] Rx_OUT,
  output [3:0] Ry_OUT,
  output [31:0] PC_1_OFFSET_OUT
);

  Register #(.width(32)) PC_1 (.D(PC_1_IN), .en(EN), .Q(PC_1_OUT), .clk(Clock));  // open: clr
  Register #(.width(32)) RESULT (.D(Result_IN), .en(EN), .Q(Result_Out), .clk(Clock));  // open: clr
  Register #(.width(32)) RAM (.D(DATA_IN), .en(EN), .Q(DATA_OUT), .clk(Clock));  // open: clr
  Register #(.width(4)) OPCODE (.D(OPCODE_IN), .en(EN), .Q(OPCODE_OUT), .clk(Clock));  // open: clr
  Register #(.width(4)) Rx (.D(Rx_In), .en(EN), .Q(Rx_OUT), .clk(Clock));  // open: clr
  Register #(.width(4)) Ry (.D(Ry_In), .en(EN), .Q(Ry_OUT), .clk(Clock));  // open: clr
  Register #(.width(32)) PC_1_2 (.D(PC_1_OFFSET_IN), .en(EN), .Q(PC_1_OFFSET_OUT), .clk(Clock));  // open: clr

  // Other names for the same wires on the sheet: CLK = Clock
endmodule

module ALU (
  input  [31:0] A,
  input  [31:0] B,
  input  [1:0] func,
  output [31:0] out,
  output [4:0] out_5,
  output [1:0] shiftmode
);

  wire [31:0] adder_1_out, adder_2_out, and_1_out, multiplexer_1_out, not_1_out, shifter_1_out,
       shifter_2_out, shifter_3_out;

  Bit_Extender #(.in_width(32), .out_width(5)) bit_extender_1 (.in(B), .out(out_5));
  assign and_1_out = A & B;  // AND_Gate and_1, 32 bits wide
  Adder #(.width(32)) adder_1 (.a(A), .b(B), .out(adder_1_out));  // open: cin, cout
  assign not_1_out = ~and_1_out;  // NOT_Gate not_1, 32 bits wide
  Adder #(.width(32)) adder_2 (.a(A), .b(32'h1), .out(adder_2_out));  // open: cin, cout
  Shifter #(.width(32)) shifter_1 (.in(A), .\dist (out_5), .out(shifter_1_out));
  Shifter #(.width(32), .shift("lr")) shifter_2 (.in(A), .\dist (out_5), .out(shifter_2_out));
  Shifter #(.width(32), .shift("ar")) shifter_3 (.in(A), .\dist (out_5), .out(shifter_3_out));
  Multiplexer #(.select(2), .width(32), .disabled(0), .enable("false")) multiplexer_1 (
    .in0(shifter_1_out), .in1(shifter_2_out), .in2(shifter_1_out), .in3(shifter_3_out),
    .out(multiplexer_1_out), .sel(B[19:18]));
  Multiplexer #(.select(2), .width(32), .disabled(0), .enable("false")) multiplexer_2 (
    .in0(adder_1_out), .in1(not_1_out), .in2(adder_2_out), .in3(multiplexer_1_out), .out(out), .sel(func));

  assign shiftmode = B[19:18];

  // Other names for the same wires on the sheet: shift_mode[1:0] = B[19:18]
endmodule

module FORWARDING (
  input  [31:0] Result_EX,
  input  [31:0] DATA_MEM,
  input  [31:0] OUT1,
  input  [3:0] Rx_EX,
  input  [3:0] OPCODE_IF,
  input  [3:0] Rx_MEM,
  input  [3:0] OPCODE_EX,
  input  [3:0] Rx_WB,
  input  [31:0] Result_MEM,
  input  [3:0] OPCODE_MEM,
  input  [3:0] OPCODE_WB,
  input  [31:0] OUT2,
  input  [3:0] Ry_IDRR,
  input  [31:0] Result_WB,
  input  [3:0] RSel_IDRR,
  output out_16,
  output out_17,
  output mem_ffff,
  output wb_ffff,
  output pos_ex,
  output pos_mem,
  output pos_wb,
  output [31:0] FOUT2,
  output [31:0] FOUT1,
  output [1:0] f__dt1,
  output [1:0] f__dt2
);

  wire and_3_out, and_12_out, and_13_out, comparator_2_lt, comparator_3_gt, comparator_4_lt, comparator_5_eq,
       comparator_11_lt, comparator_12_gt, comparator_13_lt, comparator_14_eq, comparator_17_eq,
       comparator_18_lt, comparator_19_gt, comparator_20_lt, comparator_21_eq, EX_Forwad_Ry, EX_Rx___Ry,
       EX_Rx___Rz_Rx, MEM_Forwad_Ry, MEM_Rx____IDRR_Ry, MEM_Rx___Ry, MEM_Rx___Rz_Rx, not_1_out, not_2_out,
       not_3_out, not_4_out, not_5_out, not_6_out, not_7_out, not_8_out, not_9_out, not_10_out, not_11_out,
       not_12_out, Possible_EX_F, Possible_MEM_F, Possible_WB_F, WB_Forwad_Ry, WB_Rx____IDRR_Ry, WB_Rx___Ry,
       WB_Rx___Rz_Rx;
  wire [31:0] Result_MEM_t;

  not not_1 (not_1_out, out_16);
  not not_2 (not_2_out, out_17);
  Comparator #(.width(4)) comparator_1 (.a(Ry_IDRR), .b(4'b0000), .eq(out_16));  // open: gt, lt
  Comparator #(.width(4), .mode("unsigned")) comparator_2 (
    .a(OPCODE_EX), .b(4'b0011), .lt(comparator_2_lt));  // open: gt, eq
  Comparator #(.width(4), .mode("unsigned")) comparator_3 (
    .a(OPCODE_EX), .b(4'b0011), .gt(comparator_3_gt));  // open: eq, lt
  Comparator #(.width(4), .mode("unsigned")) comparator_4 (
    .a(OPCODE_EX), .b(4'b0111), .lt(comparator_4_lt));  // open: gt, eq
  Comparator #(.width(4)) comparator_5 (.a(OPCODE_EX), .b(4'b1000), .eq(comparator_5_eq));  // open: gt, lt
  Comparator #(.width(4)) comparator_6 (.a(Rx_EX), .b(Ry_IDRR), .eq(EX_Rx___Ry));  // open: gt, lt
  Comparator #(.width(4)) comparator_7 (.a(Rx_EX), .b(RSel_IDRR), .eq(EX_Rx___Rz_Rx));  // open: gt, lt
  and and_1 (EX_Forwad_Ry, EX_Rx___Ry, not_1_out, Possible_EX_F);
  and and_2 (pos_ex, EX_Rx___Rz_Rx, not_2_out, Possible_EX_F);
  not not_3 (not_3_out, EX_Forwad_Ry);
  not not_4 (not_4_out, MEM_Rx____IDRR_Ry);
  Comparator #(.width(4)) comparator_8 (.a(RSel_IDRR), .b(4'b0000), .eq(out_17));  // open: gt, lt
  not not_5 (not_5_out, EX_Forwad_Ry);
  Multiplexer #(.select(2), .width(32)) multiplexer_1 (
    .in0(OUT1), .in1(Result_EX), .in2(Result_MEM_t), .in3(Result_WB), .out(FOUT1), .sel(f__dt1));  // open: en
  and and_3 (and_3_out, comparator_3_gt, comparator_4_lt);
  and and_4 (MEM_Forwad_Ry, not_5_out, MEM_Rx____IDRR_Ry);
  and and_5 (WB_Forwad_Ry, not_3_out, not_4_out, WB_Rx____IDRR_Ry);
  Multiplexer #(.width(2)) multiplexer_2 (
    .in0({MEM_Forwad_Ry, EX_Forwad_Ry}), .in1({WB_Forwad_Ry, 1'b1}), .out(f__dt1), .sel(WB_Forwad_Ry));  // open: en
  or or_1 (Possible_EX_F, comparator_2_lt, and_3_out, comparator_5_eq);
  not not_6 (not_6_out, out_16);
  not not_7 (not_7_out, out_17);
  Comparator #(.width(4)) comparator_9 (.a(Rx_MEM), .b(Ry_IDRR), .eq(MEM_Rx___Ry));  // open: gt, lt
  Comparator #(.width(4)) comparator_10 (.a(Rx_MEM), .b(RSel_IDRR), .eq(MEM_Rx___Rz_Rx));  // open: gt, lt
  and and_6 (MEM_Rx____IDRR_Ry, MEM_Rx___Ry, not_6_out, Possible_MEM_F);
  and and_7 (mem_ffff, MEM_Rx___Rz_Rx, not_7_out, Possible_MEM_F);
  not not_8 (not_8_out, pos_ex);
  not not_9 (not_9_out, mem_ffff);
  Multiplexer #(.select(2), .width(32)) multiplexer_3 (
    .in0(OUT2), .in1(Result_EX), .in2(Result_MEM_t), .in3(Result_WB), .out(FOUT2), .sel(f__dt2));  // open: en
  not not_10 (not_10_out, pos_ex);
  Comparator #(.width(4), .mode("unsigned")) comparator_11 (
    .a(OPCODE_MEM), .b(4'b0011), .lt(comparator_11_lt));  // open: gt, eq
  Comparator #(.width(4), .mode("unsigned")) comparator_12 (
    .a(OPCODE_MEM), .b(4'b0011), .gt(comparator_12_gt));  // open: eq, lt
  Comparator #(.width(4), .mode("unsigned")) comparator_13 (
    .a(OPCODE_MEM), .b(4'b0111), .lt(comparator_13_lt));  // open: gt, eq
  Comparator #(.width(4)) comparator_14 (.a(OPCODE_MEM), .b(4'b1000), .eq(comparator_14_eq));  // open: gt, lt
  not not_11 (not_11_out, out_16);
  not not_12 (not_12_out, out_17);
  and and_8 (pos_mem, not_10_out, mem_ffff);
  and and_9 (pos_wb, not_8_out, not_9_out, wb_ffff);
  Multiplexer #(.width(2)) multiplexer_4 (
    .in0({pos_mem, pos_ex}), .in1({pos_wb, 1'b1}), .out(f__dt2), .sel(pos_wb));  // open: en
  Comparator #(.width(4)) comparator_15 (.a(Rx_WB), .b(Ry_IDRR), .eq(WB_Rx___Ry));  // open: gt, lt
  Comparator #(.width(4)) comparator_16 (.a(Rx_WB), .b(RSel_IDRR), .eq(WB_Rx___Rz_Rx));  // open: gt, lt
  and and_10 (WB_Rx____IDRR_Ry, WB_Rx___Ry, not_11_out, Possible_WB_F);
  and and_11 (wb_ffff, WB_Rx___Rz_Rx, not_12_out, Possible_WB_F);
  Multiplexer #(.width(32)) multiplexer_5 (
    .in0(Result_MEM), .in1(DATA_MEM), .out(Result_MEM_t), .sel(comparator_17_eq));  // open: en
  Comparator #(.width(4)) comparator_17 (.a(OPCODE_MEM), .b(4'b0101), .eq(comparator_17_eq));  // open: gt, lt
  and and_12 (and_12_out, comparator_12_gt, comparator_13_lt);
  or or_2 (Possible_MEM_F, comparator_11_lt, and_12_out, comparator_14_eq);
  Comparator #(.width(4), .mode("unsigned")) comparator_18 (
    .a(OPCODE_WB), .b(4'b0011), .lt(comparator_18_lt));  // open: gt, eq
  Comparator #(.width(4), .mode("unsigned")) comparator_19 (
    .a(OPCODE_WB), .b(4'b0011), .gt(comparator_19_gt));  // open: eq, lt
  Comparator #(.width(4), .mode("unsigned")) comparator_20 (
    .a(OPCODE_WB), .b(4'b0111), .lt(comparator_20_lt));  // open: gt, eq
  Comparator #(.width(4)) comparator_21 (.a(OPCODE_WB), .b(4'b1000), .eq(comparator_21_eq));  // open: gt, lt
  and and_13 (and_13_out, comparator_19_gt, comparator_20_lt);
  or or_3 (Possible_WB_F, comparator_18_lt, and_13_out, comparator_21_eq);

  // Other names for the same wires on the sheet: EX_Rx____IDRR_Ry = EX_Forwad_Ry; EX_Forwad_Rz_Rx = pos_ex;
  //   EX_Rx____IDRR_Rz_Rx = pos_ex; MEM_Forwad_Rz_Rx = pos_mem; WB_Forwad_Rz_Rx = pos_wb;
  //   MEM_Rx____IDRR_Rz_Rx = mem_ffff; Result_MEM_0[31:0] = Result_MEM; ResultSel_Ry[1:0] = f__dt1;
  //   ResultSel_Rz_Rx[1:0] = f__dt2; rx_rz__0 = out_17; ry__0 = out_16; Rz_Rx_IDRR[3:0] = RSel_IDRR;
  //   WB_Rx____IDRR_Rz_Rx = wb_ffff
endmodule
